# Fritzing sketch perfboard (saved by Fritzing 0.9.3b)
circuit board: 8.46667cm x 5.64444cm
stripboards: 1

parts:
  Q2 = Basic FET N-Channel [package="D2Pak [SMD]"]
  J1 = Camdenboss CTB0158-2 [part_number=CTB0158-2 package=THT]  # not connected
  U3 = atmega328 [package=dip]
  Y3 = Resonator [frequency="16 Mhz" package=THT]  # not connected
  PBRESET = Momentary Switch [package=ksa_sealed_tac_switch]
  R16 = Resistor [tolerance=±5% resistance=10k package=THT]
  R17 = Resistor [tolerance=±5% resistance=10k package=THT]
  R18 = Resistor [tolerance=±5% resistance=10k package=THT]
  R19 = Resistor [tolerance=±5% resistance=10k package=THT]
  JP3 = Header 3 [package=molex-1x3_lock]
  Display = female pin header, 4 pins [form="♀ (female)"]
  SERIAL = female pin header, 6 pins [form="♀ (female)"]
  Therm = female pin header, 5 pins [form="♀ (female)"]
  R20 = Resistor [tolerance=±5% resistance=10k package=THT]
  C6 = Ceramic Capacitor [capacitance="100 nF" package="1206 [SMD, multilayer]"]
  EXT = female pin header, 3 pins [form="♀ (female)"]
  Q4 = NPN-Transistor [package="TO92 [THT]"]
  Q5 = NPN-Transistor [package="TO92 [THT]"]
  SDCARD = female pin header, 8 pins [form="♀ (female)"]
  Poti = female pin header, 5 pins [form="♀ (female)"]
  J10 = Camdenboss CTB0158-2 [part_number=CTB0158-2 package=THT]  # not connected
  J11 = Power Jack [package=power_jack_slot]  # not connected
  J12 = Power Jack [package=power_jack_slot]  # not connected
  Q6 = NPN-Transistor [package="TO92 [THT]"]
  Q7 = NPN-Transistor [package="TO92 [THT]"]
  CAMERA = female pin header, 3 pins [form="♀ (female)"]
  BUCKCONV = female pin header, 5 pins [form="♀ (female)"]
  PBSELECT = Momentary Switch [package=ksa_sealed_tac_switch]
  R21 = Resistor [tolerance=±5% resistance=10k package=THT]  # not connected
  BALANCE1 = female pin header, 2 pins [form="♀ (female)"]
  BALANCE2 = female pin header, 2 pins [form="♀ (female)"]

nets (from the breadboard view):
  N1: Q2.Gate, U3.D7
  N2: Q2.source, JP3.3, BUCKCONV.pin4
  N3: U3.RESET, PBRESET.2, R20.Pin_1, C6.1
  N4: U3.D0_(RX), SERIAL.pin4
  N5: U3.D1_(TX), SERIAL.pin5, SERIAL.pin6, C6.0
  N6: U3.D4, Q6.B
  N7: U3.VCC, SERIAL.pin3, R20.Pin_0, PBSELECT.2
  N8: U3.GND, SERIAL.pin1, SERIAL.pin2
  N9: U3.XLAT1, U3.XLAT2
  N10: U3.D6_(PWM), Q7.B
  N11: U3.D8, Q5.B
  N12: U3.D9_(PWM), Q4.B
  N13: U3.D10_(PWM), SDCARD.pin2
  N14: U3.D11_(PWM), SDCARD.pin3
  N15: U3.D12, SDCARD.pin4
  N16: U3.D13, SDCARD.pin5
  N17: U3.AVCC, U3.AREF, Display.pin2, Therm.pin1, EXT.pin2, SDCARD.pin8, Poti.pin1, BUCKCONV.pin5
  N18: U3.A0, BALANCE2.pin1
  N19: U3.A1, BALANCE2.pin2
  N20: U3.A2, Poti.pin3
  N21: U3.A3, EXT.pin1
  N22: U3.A4, Display.pin3, Therm.pin2
  N23: U3.A5, Display.pin4, Therm.pin3
  N24: R16.Pin_0, JP3.1
  N25: R16.Pin_1, R18.Pin_0, BALANCE1.pin2
  N26: R17.Pin_0, JP3.2
  N27: R17.Pin_1, R19.Pin_0, BALANCE1.pin1
  N28: R18.Pin_1, R19.Pin_1
  N29: Display.pin1, Q4.C, SDCARD.pin6, Poti.pin5
  N30: Therm.pin5, EXT.pin3, Q5.C
  N31: Q4.E, Q5.E
  N32: Q6.E, Q7.E, CAMERA.pin1
  N33: Q6.C, CAMERA.pin3
  N34: Q7.C, CAMERA.pin2
